// Logisim project program1.circ as structural Verilog: 1 circuit, main circuit main
module main (
  input  X,
  input  Y,
  input  X_2,
  input  Y_2,
  input  X_3,
  input  X_4,
  input  Y_3,
  input  X_5,
  input  Y_4,
  output X_Y,
  output X_Y_2,
  output nX,
  output nX_Y,
  output X_Y_3
);

  or or_1 (X_Y, X, Y);
  and and_1 (X_Y_2, X_2, X_2, Y_2);
  not not_1 (nX, X_3);
  xor xor_1 (nX_Y, X_4, Y_3);
  xnor xnor_1 (X_Y_3, X_5, Y_4);
endmodule
