// Logisim project program19.circ as structural Verilog: 1 circuit, main circuit main
module main (
  input  A,
  input  B,
  input  C_IN,
  input  [1:0] in_4,
  output RESULT,
  output C_OUT
);

  wire adder_1_out, and_1_out, or_1_out;

  or or_1 (or_1_out, A, B);
  and and_1 (and_1_out, A, B);
  Adder #(.width(1)) adder_1 (.a(A), .b(B), .out(adder_1_out), .cin(C_IN), .cout(C_OUT));
  Multiplexer #(.select(2)) multiplexer_1 (
    .in0(or_1_out), .in1(and_1_out), .in2(adder_1_out), .out(RESULT), .sel(in_4));  // open: in3, en
endmodule
