// Logisim project program2.circ as structural Verilog: 1 circuit, main circuit main
module main (
  input  X,
  input  Y,
  input  X_2,
  input  Y_2,
  input  in_5,
  output out_6,
  output out_7,
  output out_8
);

  wire nand_1_out, nand_2_out, nand_3_out;

  nand nand_1 (nand_1_out, X, Y);
  nand nand_2 (nand_2_out, X_2, X_2);
  nand nand_3 (nand_3_out, Y_2, Y_2);
  nand nand_4 (out_8, in_5, in_5);
  nand nand_5 (out_6, nand_1_out, nand_1_out);
  nand nand_6 (out_7, nand_2_out, nand_3_out);

  // Notes on the sheet:
  //   '(X,Y)
  //   'X+'Y
  //   'X+'Y
  //   'X
  //   'Y
  //   X,Y
  //   X+Y
endmodule
